# Fritzing sketch asentry (saved by Fritzing 0.9.3b)

parts:
  Part1 = Adafruit OLED Monochrome 1.3in 128x64 with STEMMA QT [part_number="Adafruit #938"]
  Mod1 = Raspberry Pi Pico W  # not connected
  S1 = Round Pushbutton
  Part2 = Adafruit I2S Amp BFF [part_number="Adafruit #5770"]
  Adafruit_PiCowbell_Proto_for_Pico1 = Adafruit PiCowbell Proto for Pico - Reset Button and STEMMA QT [part_number=#5200]
  SP1 = SPEAKER [package=pcb_mount_speaker]

nets:
  VCC: Part1.VCC, Adafruit_PiCowbell_Proto_for_Pico1.3.3V
  N1: Part1.SCL, Adafruit_PiCowbell_Proto_for_Pico1.IO5
  GND: Part1.GND, S1.leg1, Part2.GND, Adafruit_PiCowbell_Proto_for_Pico1.IO13, Adafruit_PiCowbell_Proto_for_Pico1.GND
  N2: Part1.SDA, Adafruit_PiCowbell_Proto_for_Pico1.IO4
  N3: S1.leg0, Adafruit_PiCowbell_Proto_for_Pico1.IO14
  N4: Part2.A0, Adafruit_PiCowbell_Proto_for_Pico1.AD2
  N5: Part2.A1, Adafruit_PiCowbell_Proto_for_Pico1.AD1
  N6: Part2.A2, Part2.A3, Adafruit_PiCowbell_Proto_for_Pico1.AD0
  N7: Part2.+5V, Adafruit_PiCowbell_Proto_for_Pico1.VBUS
  N8: Part2.VO+, SP1.-
  N9: Part2.VO-, SP1.+

notes:
  Stemma QT cable
  Pi Pico W is mounted on top of PiCowbell with headers - shown separately for clarity
  Molex PicoBlade cable

custom parts:
  Adafruit OLED Monochrome 1.3in 128x64 with STEMMA QT: These displays are small, only about 1.3" diagonal, but very readable due to the high contrast of an OLED display. This display is made of 128x64 individual white OLED pixels, each one is turned on or off by the controller chip. Because the display makes its own light, no backlight is required. This reduces the power required to run the OLED and is why the display has such high contrast; we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
  Raspberry Pi Pico W: Raspberry Pi Pico W. Based around the RP2040 microcontroller the Pico W is a low cost microcontroller device bringing Raspberry Pi quality, cost, and easy of use to the microcontroller space. The areas marked KEEPOUT in pcb silkscreen should not have traces running through them to avoid shorts on a soldered in module!
  Adafruit I2S Amp BFF: Our QT Py boards are a great way to make very small microcontroller projects that pack a ton of power - and now we have a way for you to add an I2S 3 Watt amplifier, for high quality audio playback, that can fit on the back of your miniature dev board. It uses just three GPIO pins that do not intersect with the I2C/UART or SPI port. We call this the Adafruit I2S Amp BFF - a "Best Friend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
  Adafruit PiCowbell Proto for Pico - Reset Button and STEMMA QT: Ding dong! Hear that? It's the PiCowbell ringing, letting you know that the new Adafruit PiCowbell Proto is finally in stock and ready to assist your Raspberry Pi Pico and Pico W project with handy hardware and practical prototyping. The PiCowbell Proto is the same size and shape as a Pico, and is intended to socket underneath to make programming and sensor connectivity easy. Reset button?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
